# Fritzing sketch circuit_diagram (saved by Fritzing 0.9.3b)
breadboards: 1

parts:
  Bauteil1 = Arduino Uno (Rev3)
  R1 = Photocell (LDR) [package=THT]
  R2 = Photocell (LDR) [package=THT]
  R5 = Resistor [tolerance=±5% resistance=220 package=THT]
  R6 = Resistor [tolerance=±5% resistance=220 package=THT]
  LED1 = LED - 5mm [color="Infrared (880nm)" package="5 mm [THT]"]
  LED4 = RGB LED (com. cathode, rgb) [package="5 mm [THT]"]
  R7 = Resistor [tolerance=±5% resistance=220 package=THT]
  R8 = Resistor [tolerance=±5% resistance=220 package=THT]
  R10 = Resistor [tolerance=±5% resistance=220 package=THT]
  R11 = Resistor [tolerance=±5% resistance=220 package=THT]
  R12 = Resistor [tolerance=±5% resistance=220 package=THT]
  X2 = X113647 Stepper Driver Board [package=board]
  M2 = 28BYJ-48 Stepper Motor
  X1 = X113647 Stepper Driver Board [package=board]
  M1 = 28BYJ-48 Stepper Motor
  LED3 = LED - 5mm [color="Infrared (880nm)" package="5 mm [THT]"]
  Grove1 = Grove Light Sensor

nets:
  N1: Bauteil1.A0, R1.pin_0, R6.Pin_1
  N2: Bauteil1.A1, R2.pin_0, R5.Pin_1
  N3: Bauteil1.A2, Grove1.SIG
  N4: Bauteil1.D8, X1.IN4
  N5: Bauteil1.D9_PWM, X2.IN1
  N6: Bauteil1.D10_PWM/SS, X2.IN2
  N7: Bauteil1.D11_PWM/MOSI, X2.IN3
  N8: Bauteil1.D12/MISO, X2.IN4
  GND: Bauteil1.GND, R1.pin_1, R2.pin_1, LED1.cathode, LED4.common_cathode, X2.GND, X1.GND, LED3.cathode, Grove1.GND
  N9: Bauteil1.D2, R10.Pin_1
  N10: Bauteil1.D3_PWM, R12.Pin_1
  N11: Bauteil1.D4, R11.Pin_1
  N12: Bauteil1.D5_PWM, X1.IN1
  N13: Bauteil1.D6_PWM, X1.IN2
  N14: Bauteil1.D7, X1.IN3
  5V: Bauteil1.5V, R5.Pin_0, R6.Pin_0, R7.Pin_0, R8.Pin_0, X2.+V, X1.+V, Grove1.VCC
  N15: LED1.anode, R8.Pin_1
  N16: LED4.red_anode, R11.Pin_0
  N17: LED4.green_anode, R12.Pin_0
  N18: LED4.blue_anode, R10.Pin_0
  N19: R7.Pin_1, LED3.anode
  N20: X2.BLUE, M2.BLUE
  N21: X2.PINK, M2.PINK
  N22: X2.YELLOW, M2.YELLOW
  N23: X2.ORANGE, M2.ORANGE
  N24: X2.RED, M2.RED
  N25: X1.BLUE, M1.BLUE
  N26: X1.PINK, M1.PINK
  N27: X1.YELLOW, M1.YELLOW
  N28: X1.ORANGE, M1.ORANGE
  N29: X1.RED, M1.RED

custom parts:
  X113647 Stepper Driver Board: A common stepper motor driver board based on ULN2003APG darlington array
